# Fritzing sketch LED Button (saved by Fritzing 0.9.10b)
breadboards: 1

parts:
  LED1 = LED - 5mm [color="Red (633nm)" current=0.030 package="5 mm [THT]"]
  R1 = Resistor [tolerance=±5% power=0.25 resistance=220 package=THT]
  S1 = Pushbutton [package="[THT]"]
  VCC1 = 4 x AAA Battery Mount

nets:
  N1: LED1.cathode, R1.Pin_1
  N2: LED1.anode, S1.Pin_3, S1.Pin_4
  N3: R1.Pin_0, VCC1.-
  N4: S1.Pin_1, S1.Pin_2, VCC1.+
