# Fritzing sketch Ohms law (saved by Fritzing 0.9.10b)
breadboards: 1

parts:
  VCC1 = Battery
  R1 = Resistor [tolerance=±5% power=0.25 resistance=220 package=THT]
  VM1 = Multimeter (DC Voltage)
  AM1 = Multimeter (DC Current)

nets:
  N1: VCC1.-, VM1.COM_Probe, AM1.COM_Probe
  N2: VCC1.+, R1.Pin_1, VM1.V_Probe
  N3: R1.Pin_0, AM1.A_Probe
