# Fritzing sketch Resistors and voltage divider (saved by Fritzing 0.9.10b)
breadboards: 3

parts:
  R1 = Resistor [tolerance=±5% power=0.25 resistance=220 package=THT]
  R3 = Resistor [tolerance=±5% power=0.25 resistance=220 package=THT]
  R4 = Resistor [tolerance=±5% power=0.25 resistance=220 package=THT]
  OM1 = Multimeter (Ohmmeter)
  OM2 = Multimeter (Ohmmeter)
  R5 = Resistor [tolerance=±5% power=0.25 resistance=220 package=THT]
  R6 = Resistor [tolerance=±5% power=0.25 resistance=220 package=THT]
  OM3 = Multimeter (DC Voltage)
  VM1 = Multimeter (DC Voltage)
  VCC1 = Battery
  R2 = Resistor [tolerance=±5% power=0.25 resistance=220 package=THT]

nets:
  N1: R1.Pin_0, OM1.COM_Probe, R2.Pin_0
  N2: R1.Pin_1, OM1.V_Probe, R2.Pin_1
  N3: R3.Pin_0, OM2.COM_Probe
  N4: R3.Pin_1, R4.Pin_0
  N5: R4.Pin_1, OM2.V_Probe
  N6: R5.Pin_0, OM3.COM_Probe, VCC1.-
  N7: R5.Pin_1, R6.Pin_0, VM1.COM_Probe
  N8: R6.Pin_1, OM3.V_Probe, VM1.V_Probe, VCC1.+
