# Fritzing sketch potentiometer light (saved by Fritzing 0.9.10b)
breadboards: 1

parts:
  VCC1 = 4 x AAA Battery Mount
  R1 = Rotary Potentiometer (Small) [maximum_resistance=100kΩ knob_status=0% power=0.5W package=THT]
  R2 = Resistor [tolerance=±5% power=0.25 resistance=220 package=THT]
  LED1 = LED - 3mm [color="Red (633nm)" current=30mA package="3 mm [THT]"]

nets:
  N1: VCC1.-, R1.leg2, R2.Pin_1
  N2: VCC1.+, R1.leg1
  N3: R1.wiper, LED1.anode
  N4: R2.Pin_0, LED1.cathode
