# Fritzing sketch potentiometer_measure (saved by Fritzing 0.9.10b)
breadboards: 1

parts:
  VCC1 = 4 x AAA Battery Mount
  R1 = Rotary Potentiometer (Small) [maximum_resistance=100kΩ knob_status=75% power=0.5W package=THT]
  P1 = Multimeter straight red probe
  P2 = Multimeter straight black probe
  AM1 = Multimeter (DC Current)
  R2 = Resistor [tolerance=±5% power=0.25 resistance=220 package=THT]
  LED1 = LED - 3mm [color="Red (633nm)" current=30mA package="3 mm [THT]"]
  P3 = Multimeter straight black probe
  VM1 = Multimeter (DC Voltage)

nets:
  N1: VCC1.-, R1.leg2, R2.Pin_1, P3.Probe_tip, P3.Probe_meter_end, P3.Probe_tip_2, VM1.COM_Probe
  N2: VCC1.+, R1.leg1
  N3: R1.wiper, P1.Probe_tip, P1.Probe_meter_end, P1.Probe_tip_2, AM1.A_Probe, VM1.V_Probe
  N4: P2.Probe_tip, P2.Probe_meter_end, P2.Probe_tip_2, AM1.COM_Probe, LED1.anode
  N5: R2.Pin_0, LED1.cathode
