# Fritzing sketch read toggle switch (saved by Fritzing 0.9.10b)
breadboards: 1

parts:
  VCC1 = 4 x AAA Battery Mount
  R1 = Resistor [tolerance=±5% power=0.25 resistance=220 package=THT]
  LED1 = LED - 5mm [color="Red (633nm)" current=0.030 package="5 mm [THT]"]
  LED2 = LED - 5mm [color="Red (633nm)" current=0.030 package="5 mm [THT]"]
  S1 = Toggle Switch [package=THT]

nets:
  N1: VCC1.-, R1.Pin_0
  N2: VCC1.+, LED1.anode, LED2.anode
  N3: R1.Pin_1, S1.COM
  N4: LED1.cathode, S1.L1
  N5: LED2.cathode, S1.L2
