# Fritzing sketch IR controls motor (saved by Fritzing 0.9.10b)
breadboards: 1

parts:
  M1 = DC Motor [voltage_(max)=6V voltage_(min)=3V]
  Q1 = NPN-Transistor [package="TO92 [THT]"]
  Q2 = NPN-Transistor [package="TO92 [THT]"]
  R1 = Resistor [tolerance=±5% power=0.25 resistance=150 package=THT]
  VCC1 = 4 x AAA Battery Mount
  M2 = fc-51 [package=THT]

nets:
  5V: M1.pin_1, VCC1.+, M2.pin3
  N1: M1.pin_2, Q1.C, Q2.C
  N2: Q1.E, Q2.B
  N3: Q1.B, R1.Pin_1
  GND: Q2.E, VCC1.-, M2.pin2
  N4: R1.Pin_0, M2.pin1
