# Fritzing sketch analog sensor test (saved by Fritzing 0.9.10b)
breadboards: 1

parts:
  J1 = Infrared Proximity Sensor [distance_to_obstacle=5%]
  VM1 = Multimeter (DC Voltage)
  LED1 = LED - 5mm [color="Red (633nm)" current=0.030 package="5 mm [THT]"]
  R1 = Resistor [tolerance=±5% power=0.25 resistance=22 package=THT]
  VCC1 = 4 x AAA Battery Mount

nets:
  N1: J1.Vout, VM1.V_Probe, LED1.anode
  GND: J1.GND, VM1.COM_Probe, R1.Pin_0, VCC1.-
  5V: J1.Vcc, VCC1.+
  N2: LED1.cathode, R1.Pin_1
