# Fritzing sketch detector test (saved by Fritzing 0.9.10b)
breadboards: 1

parts:
  LED1 = LED - 5mm [color="Red (633nm)" current=0.030 package="5 mm [THT]"]
  VCC1 = 4 x AAA Battery Mount
  R1 = Resistor [tolerance=±5% power=0.25 resistance=47 package=THT]
  M1 = fc-51 [package=THT]

nets:
  GND: LED1.cathode, VCC1.-, M1.pin2
  N1: LED1.anode, M1.pin1
  5V: VCC1.+, R1.Pin_1
  N2: R1.Pin_0, M1.pin3
