# Fritzing sketch h bridge (saved by Fritzing 0.9.10b)
breadboards: 1

parts:
  M1 = DC Motor [voltage_(max)=6V voltage_(min)=3V]
  VCC1 = 4 x AAA Battery Mount
  S4 = Pushbutton [package=THT]
  S3 = Pushbutton [package=THT]
  S1 = Pushbutton [package=THT]
  S2 = Pushbutton [package=THT]

nets:
  N1: M1.pin_1, S4.leg1, S1.leg1
  N2: M1.pin_2, S3.leg1, S2.leg1
  GND: VCC1.-, S3.leg0, S1.leg0
  5V: VCC1.+, S4.leg0, S2.leg0
