# Fritzing sketch Exercise2 (saved by Fritzing 0.9.10b)
breadboards: 1

parts:
  Part1 = Arduino Leonardo (Rev3b)
  S1 = Pushbutton [package="[THT]"]
  R1 = Resistor [tolerance=±5% power=0.25 resistance=220 package=THT]

nets:
  N1: Part1.D3_PWM/SCL, Part1.SCL, S1.Pin_3, S1.Pin_4, R1.Pin_0
  5V: Part1.5V, S1.Pin_1, S1.Pin_2
  GND: Part1.GND, R1.Pin_1
