# Fritzing sketch Exercise3 (saved by Fritzing 0.9.10b)
breadboards: 1

parts:
  Part1 = Arduino Leonardo (Rev3b)
  LED1 = LED - 5mm [color="Red (633nm)" current=0.030 package="5 mm [THT]"]
  R1 = Resistor [tolerance=±5% power=0.25 resistance=100 package=THT]
  R2 = Rotary Potentiometer (Small) [maximum_resistance=100kΩ knob_status=50% power=0.5W package=THT]

nets:
  N1: Part1.D5_PWM, LED1.anode
  5V: Part1.5V, R2.leg1
  GND: Part1.GND, R1.Pin_1, R2.leg2
  N2: Part1.A5, R2.wiper
  N3: LED1.cathode, R1.Pin_0
